# Fritzing sketch PIRRelayMega9V (saved by Fritzing 0.9.2b)

parts:
  U1 = RELAY [package=relay-jzc]
  BC338 = TRANSISTOR_NPN_2 [package=to-92]
  part = Resistor [tolerance=±5% resistance=1k package="1206 [SMD]"]
  D3 = Rectifier Diode [part_number=Rectifier package="Melf DO-213 AA [SMD]"]
  part_2 = Resistor [tolerance=±5% resistance=10k package="1206 [SMD]"]
  PIR1 = PIR sensor
  Part4 = Arduino Mega 2560 (Rev3)
  part_3 = Battery block 9V

nets:
  VCC: U1.COIL2, D3.cathode, part_2.Pin_0, PIR1.VCC, Part4.5V
  N1: U1.COIL1, BC338.C, D3.anode
  N2: BC338.B, part.Pin_0
  GND: BC338.E, PIR1.GND, Part4.GND, part_3.-
  N3: part.Pin_1, Part4.D4_PWM
  N4: part_2.Pin_1, PIR1.SIG, Part4.D7_PWM
  N5: Part4.VIN, part_3.+
